// Logisim project 2_bit_Divider.circ as structural Verilog: 1 circuit, main circuit main
module main (
  input  A2,
  input  A1,
  input  B2,
  input  B1,
  output Q1,
  output Q2
);

  wire and_1_out, and_2_out, and_3_out, and_4_out, and_5_out, and_6_out, not_1_out, not_2_out, not_3_out,
       not_4_out, not_5_out, not_6_out, not_7_out;

  not not_1 (not_1_out, B1);
  not not_2 (not_2_out, B2);
  not not_3 (not_3_out, B2);
  not not_4 (not_4_out, B1);
  not not_5 (not_5_out, B2);
  not not_6 (not_6_out, B1);
  not not_7 (not_7_out, B2);
  and and_1 (and_1_out, not_1_out, not_2_out);
  and and_2 (and_2_out, not_3_out, A1);
  and and_3 (and_3_out, not_4_out, A2);
  and and_4 (and_4_out, A1, A2);
  and and_5 (and_5_out, not_5_out, not_6_out);
  and and_6 (and_6_out, not_7_out, A2);
  or or_1 (Q1, and_1_out, and_2_out, and_3_out, and_4_out);
  or or_2 (Q2, and_5_out, and_6_out);

  // Notes on the sheet:
  //   A2: 0 0 1 1 0 0 1 1 0 0 1 1 0 0 1 1
  //   _________________________
  //   A1: 0 1 0 1 0 1 0 1 0 1 0 1 0 1 0 1
  //   _________________________
  //   B2: 0 0 0 0 0 0 0 0 1 1 1 1 1 1 1 1
  //   _________________________
  //   B1: 0 0 0 0 1 1 1 1 0 0 0 0 1 1 1 1
  //   _________________________
  //   _________________________
  //   Q1: 1 1 1 1 0 0 1 1 0 0 0 0 0 0 0 0
  //   _________________________
  //   Q2: 1 1 1 1 0 0 1 1 0 0 0 0 0 0 0 0
  //   Q1 = B2'B1' + A1B2' + A2B1' + A2A1
  //   Q2 = B2'B1' + A2B2'
endmodule
