// Logisim project Divider.circ as structural Verilog: 5 circuits, main circuit main
module main (
  input  d,
  input  c,
  input  b,
  input  a,
  output q0,
  output q1
);

  wire and_1_out, and_2_out, and_3_out, and_4_out, and_5_out, and_6_out, not_1_out, not_2_out, not_3_out,
       not_4_out, not_5_out, not_6_out, not_7_out, undriven;

  not not_1 (not_1_out, b);
  not not_2 (not_2_out, a);
  not not_3 (not_3_out, c);
  not not_4 (not_4_out, b);
  not not_5 (not_5_out, b);
  not not_6 (not_6_out, a);
  not not_7 (not_7_out, b);
  and and_1 (and_1_out, not_1_out, c, undriven);
  and and_2 (and_2_out, not_2_out, b, not_3_out);
  and and_3 (and_3_out, a, not_4_out, undriven);
  and and_4 (and_4_out, a, not_5_out, c);
  and and_5 (and_5_out, not_6_out, b, c);
  and and_6 (and_6_out, a, not_7_out);
  or or_1 (q0, and_1_out, and_2_out, and_3_out, and_4_out);
  or or_2 (q1, and_5_out, and_6_out);
endmodule

module _2_bit_divider (
  input  A2,
  input  A1,
  input  B2,
  input  B1,
  output Q1,
  output Q2
);

  wire and_1_out, and_2_out, and_3_out, and_4_out, and_5_out, and_6_out, not_1_out, not_2_out, not_3_out,
       not_4_out, not_5_out, not_6_out, not_7_out;

  not not_1 (not_1_out, B1);
  not not_2 (not_2_out, B2);
  not not_3 (not_3_out, B2);
  not not_4 (not_4_out, B1);
  not not_5 (not_5_out, B2);
  not not_6 (not_6_out, B1);
  not not_7 (not_7_out, B2);
  and and_1 (and_1_out, not_1_out, not_2_out);
  and and_2 (and_2_out, not_3_out, A1);
  and and_3 (and_3_out, not_4_out, A2);
  and and_4 (and_4_out, A1, A2);
  and and_5 (and_5_out, not_5_out, not_6_out);
  and and_6 (and_6_out, not_7_out, A2);
  or or_1 (Q1, and_1_out, and_2_out, and_3_out, and_4_out);
  or or_2 (Q2, and_5_out, and_6_out);

  // Notes on the sheet:
  //   A2: 0 0 1 1 0 0 1 1 0 0 1 1 0 0 1 1
  //   _________________________
  //   A1: 0 1 0 1 0 1 0 1 0 1 0 1 0 1 0 1
  //   _________________________
  //   B2: 0 0 0 0 0 0 0 0 1 1 1 1 1 1 1 1
  //   _________________________
  //   B1: 0 0 0 0 1 1 1 1 0 0 0 0 1 1 1 1
  //   _________________________
  //   _________________________
  //   Q1: 1 1 1 1 0 0 1 1 0 0 0 0 0 0 0 0
  //   _________________________
  //   Q2: 1 1 1 1 0 0 1 1 0 0 0 0 0 0 0 0
  //   Q1 = B2'B1' + A1B2' + A2B1' + A2A1
  //   Q2 = B2'B1' + A2B2'
endmodule

module _3_bit_divider (
  input  a,
  input  b,
  input  c,
  input  d,
  input  e,
  input  f,
  output out_7,
  output out_8,
  output out_9
);

  wire and_1_out, and_2_out, not_1_out, not_2_out, not_3_out, not_4_out, not_5_out;

  not not_1 (not_1_out, d);
  not not_2 (not_2_out, e);
  not not_3 (not_3_out, f);
  and and_1 (and_1_out, not_1_out, not_2_out, not_3_out);
  not not_4 (not_4_out, e);
  not not_5 (not_5_out, d);
  and and_2 (and_2_out, a, not_5_out, not_4_out);
  _2_bit_divider u_2_bit_divider_1 (.A2(b), .A1(c), .B2(e), .B1(f), .Q1(out_7), .Q2(out_8));
  or or_1 (out_9, and_2_out, and_1_out);
endmodule

module _4_bit_divider (
  input  A4,
  input  A3,
  input  A2,
  input  A1,
  input  B4,
  input  B3,
  input  B2,
  input  B1
);

  wire _0000_out, _0001_out, _0010_out, _0011_out, and_1_out, and_2_out, and_3_out, and_4_out, and_5_out,
       and_6_out, and_7_out, and_8_out, and_9_out, and_10_out, and_11_out, and_12_out, n3_1_q0, n3_1_q1,
       n3_1_q2, not_1_out, not_2_out, not_3_out, not_4_out, not_5_out, not_6_out, not_7_out, not_8_out,
       not_9_out, not_10_out, not_11_out, not_12_out;

  not not_1 (not_1_out, B1);
  not not_2 (not_2_out, B2);
  not not_3 (not_3_out, B3);
  not not_4 (not_4_out, B4);
  not not_5 (not_5_out, B2);
  not not_6 (not_6_out, B3);
  not not_7 (not_7_out, B4);
  not not_8 (not_8_out, B1);
  not not_9 (not_9_out, B3);
  not not_10 (not_10_out, B4);
  not not_11 (not_11_out, B3);
  not not_12 (not_12_out, B4);
  and _0000 (_0000_out, not_1_out, not_2_out, not_3_out, not_4_out);
  and _0001 (_0001_out, B1, not_5_out, not_6_out, not_7_out);
  and _0010 (_0010_out, not_8_out, B2, not_9_out, not_10_out);
  and _0011 (_0011_out, B1, B2, not_11_out, not_12_out);
  and and_1 (and_1_out, _0001_out, A1);
  and and_2 (and_2_out, _0001_out, A2);
  and and_3 (and_3_out, _0001_out, A3);
  and and_4 (and_4_out, _0001_out, A4);
  and and_5 (and_5_out, _0010_out, A2);
  and and_6 (and_6_out, _0010_out, A3);
  and and_7 (and_7_out, _0010_out, A4);
  and and_8 (and_8_out, _0010_out, 1'b0);
  and and_9 (and_9_out, _0011_out, A1);
  and and_10 (and_10_out, _0011_out, A2);
  and and_11 (and_11_out, _0011_out, A3);
  and and_12 (and_12_out, _0011_out, A4);
  _3 u_3_1 (
    .A0(and_9_out), .A1(and_10_out), .A2(and_11_out), .A3(and_12_out), .q0(n3_1_q0), .q1(n3_1_q1),
    .q2(n3_1_q2));
endmodule

module _3 (
  input  A0,
  input  A1,
  input  A2,
  input  A3,
  output q0,
  output q1,
  output q2
);

  wire and_1_out, and_2_out, and_3_out, and_4_out, and_5_out, not_1_out, not_2_out, not_3_out, not_4_out,
       not_5_out;

  not not_1 (not_1_out, A2);
  not not_2 (not_2_out, A1);
  not not_3 (not_3_out, A3);
  not not_4 (not_4_out, A1);
  not not_5 (not_5_out, A2);
  and and_1 (and_1_out, not_1_out, A1, A0);
  and and_2 (and_2_out, not_2_out, A2, not_3_out);
  and and_3 (and_3_out, A3, not_4_out, A0);
  and and_4 (and_4_out, A3, not_5_out, A1);
  and and_5 (and_5_out, A0, A1, A3);
  or or_1 (q0, and_1_out, and_2_out, and_3_out, and_4_out, and_5_out);
  // OR_Gate or_2 has open pins: out=q1
  // AND_Gate and_6 has open pins: out=q2

  // Notes on the sheet:
  //   A0A1A2A3
endmodule
