// Logisim project Divider_new_way.circ as structural Verilog: 28 circuits, main circuit Build
module Build (
  input  E,
  input  [3:0] A,
  input  [3:0] B,
  input  Clear,
  output [3:0] Q,
  output Remainder
);

  wire and_1_out, and_2_out, Ch_overflow, comparator_1_lt, comparator_2_eq, comparator_3_eq, comparator_4_gt,
       Locker_q, not_1_out, not_2_out, not_3_out, not_4_out, not_5_out, not_6_out, or_1_out, or_2_out,
       Over_Lock_q;
  wire [3:0] Ch_output, multiplexer_1_out, n4_bit_counter_1_o, R_output, subtractor_1_out;

  Hex_Digit_Display hex_digit_display_1 (.value(A));  // open: dp
  Hex_Digit_Display hex_digit_display_2 (.value(B));  // open: dp
  Comparator_part #(.width(4), .mode("unsigned")) comparator_1 (.a(A), .b(B), .lt(comparator_1_lt));  // open: gt, eq
  D_Flip_Flop #(.trigger("high")) Locker (
    .clk(or_2_out), .D(or_2_out), .Q(Locker_q), .en(E), .reset(Clear));  // open: Qn, preset
  not not_1 (not_1_out, comparator_2_eq);
  not not_2 (not_2_out, Locker_q);
  and and_1 (and_1_out, E, not_2_out, not_3_out);
  not not_3 (not_3_out, comparator_1_lt);
  Hex_Digit_Display hex_digit_display_3 (.value(R_output));  // open: dp
  Looper R (
    .Increment(4'b0001), .Enable_Input(not_1_out), .Enable_Loop(and_1_out), .Clear(comparator_2_eq),
    .Output(R_output));  // open: Overflow
  Hex_Digit_Display hex_digit_display_4 (.value(n4_bit_counter_1_o));  // open: dp
  _4_bit_Counter u_4_bit_counter_1 (.D(comparator_2_eq), .O(n4_bit_counter_1_o), .Enable(E), .Clear(Clear));
  Comparator_part #(.width(4), .mode("unsigned")) comparator_2 (
    .a(R_output), .b(B), .eq(comparator_2_eq));  // open: gt, lt
  Hex_Digit_Display hex_digit_display_5 (.value(Ch_output));  // open: dp
  Looper Ch (
    .Increment(R_output), .Enable_Input(comparator_2_eq), .Enable_Loop(comparator_2_eq), .Clear(Clear),
    .Overflow(Ch_overflow), .Output(Ch_output));
  D_Flip_Flop #(.trigger("high")) Over_Lock (
    .clk(Ch_overflow), .D(Ch_overflow), .Q(Over_Lock_q), .en(E), .reset(Clear));  // open: Qn, preset
  Subtractor #(.width(4)) subtractor_1 (
    .a(n4_bit_counter_1_o), .b(4'b0001), .out(subtractor_1_out));  // open: bin, bout
  not not_4 (not_4_out, B[1]);
  not not_5 (not_5_out, B[2]);
  not not_6 (not_6_out, B[3]);
  Multiplexer #(.width(4), .disabled(0)) multiplexer_1 (
    .in0(n4_bit_counter_1_o), .in1(subtractor_1_out), .out(multiplexer_1_out), .sel(or_1_out));  // open: en
  or or_1 (or_1_out, comparator_4_gt, and_2_out, Over_Lock_q);
  Comparator_part #(.width(4), .mode("unsigned")) comparator_3 (
    .a(Ch_output), .b(A), .eq(comparator_3_eq));  // open: gt, lt
  Comparator_part #(.width(4), .mode("unsigned")) comparator_4 (
    .a(Ch_output), .b(A), .gt(comparator_4_gt));  // open: eq, lt
  and and_2 (and_2_out, B[0], not_4_out, not_5_out, not_6_out);
  _4_bit_Enabler u_4_bit_enabler_1 (.I(multiplexer_1_out), .O(Q), .Enable(E));
  or or_2 (or_2_out, comparator_3_eq, comparator_4_gt, Over_Lock_q);
  Hex_Digit_Display hex_digit_display_6 (.value(Q), .dp(or_1_out));
  and and_3 (Remainder, or_1_out, E);

  // Notes on the sheet:
  //   If B = 1
endmodule

module Looper (
  input  Enable_Input,
  input  Enable_Loop,
  input  [3:0] Increment,
  input  Clear,
  output [3:0] Output,
  output Overflow
);

  wire [3:0] adder_1_out, n4_bit_enabler_1_o, n4_bit_enabler_2_o;

  _4_bit_Enabler u_4_bit_enabler_1 (.I(Increment), .O(n4_bit_enabler_1_o), .Enable(Enable_Input));
  Register #(.width(4), .trigger("high")) register_1 (
    .D(n4_bit_enabler_2_o), .Q(Output), .clk(Enable_Input), .clr(Clear));  // open: en
  _4_bit_Enabler u_4_bit_enabler_2 (.I(adder_1_out), .O(n4_bit_enabler_2_o), .Enable(Enable_Loop));
  Adder #(.width(4)) adder_1 (.a(Output), .b(n4_bit_enabler_1_o), .out(adder_1_out), .cout(Overflow));  // open: cin
endmodule

module Build_5 (
  input  E,
  input  [3:0] A,
  input  [3:0] B,
  output [3:0] Q
);

  wire and_1_out, comparator_1_lt, comparator_2_eq, comparator_3_eq, comparator_4_eq, not_1_out, not_2_out,
       not_3_out;
  wire [3:0] adder_1_out, adder_2_out, Check_q, n4_bit_enabler_1_o, n4_bit_enabler_2_o, Result_q;

  Hex_Digit_Display hex_digit_display_1 (.value(A));  // open: dp
  Hex_Digit_Display hex_digit_display_2 (.value(B));  // open: dp
  Comparator_part #(.width(4), .mode("unsigned")) comparator_1 (.a(A), .b(B), .lt(comparator_1_lt));  // open: gt, eq
  not not_1 (not_1_out, comparator_4_eq);
  and and_1 (and_1_out, E, not_1_out, not_2_out);
  not not_2 (not_2_out, comparator_1_lt);
  Register #(.width(4), .trigger("high")) Result (
    .D(n4_bit_enabler_1_o), .en(and_1_out), .Q(Result_q), .clk(and_1_out), .clr(comparator_2_eq));
  _4_bit_Enabler u_4_bit_enabler_1 (.I(adder_1_out), .O(n4_bit_enabler_1_o), .Enable(and_1_out));
  Adder #(.width(4)) adder_1 (.a(Result_q), .b(4'b0001), .out(adder_1_out));  // open: cin, cout
  Comparator_part #(.width(4), .mode("unsigned")) comparator_2 (
    .a(Result_q), .b(B), .eq(comparator_2_eq));  // open: gt, lt
  Register #(.width(4), .trigger("high")) Check (
    .D(n4_bit_enabler_2_o), .en(comparator_2_eq), .Q(Check_q), .clk(comparator_2_eq));  // open: clr
  Comparator_part #(.width(4), .mode("unsigned")) comparator_3 (
    .a(Result_q), .b(Check_q), .eq(comparator_3_eq));  // open: gt, lt
  not not_3 (not_3_out, comparator_3_eq);
  Adder #(.width(4)) adder_2 (.a(Check_q), .b(4'b0001), .out(adder_2_out));  // open: cin, cout
  Comparator_part #(.width(4), .mode("unsigned")) comparator_4 (
    .a(Check_q), .b(A), .eq(comparator_4_eq));  // open: gt, lt
  Hex_Digit_Display hex_digit_display_3 (.value(Q));  // open: dp
  _4_bit_Counter u_4_bit_counter_1 (.D(comparator_3_eq), .O(Q), .Enable(E));  // open: Clear
  _4_bit_Enabler u_4_bit_enabler_2 (.I(adder_2_out), .O(n4_bit_enabler_2_o), .Enable(not_3_out));
endmodule

module _4_bit_Counter (
  input  Enable,
  input  D,
  input  Clear,
  output [3:0] O
);

  wire d_ff_1_qn, d_ff_2_qn, d_ff_3_qn, d_ff_4_qn;

  D_Flip_Flop d_ff_1 (.clk(D), .D(d_ff_1_qn), .Q(O[0]), .Qn(d_ff_1_qn), .en(Enable), .reset(Clear));  // open: preset
  D_Flip_Flop d_ff_2 (
    .clk(d_ff_1_qn), .D(d_ff_2_qn), .Q(O[1]), .Qn(d_ff_2_qn), .en(Enable), .reset(Clear));  // open: preset
  D_Flip_Flop d_ff_3 (
    .clk(d_ff_2_qn), .D(d_ff_3_qn), .Q(O[2]), .Qn(d_ff_3_qn), .en(Enable), .reset(Clear));  // open: preset
  D_Flip_Flop d_ff_4 (
    .clk(d_ff_3_qn), .D(d_ff_4_qn), .Q(O[3]), .Qn(d_ff_4_qn), .en(Enable), .reset(Clear));  // open: preset
endmodule

module Build_4 (
  input  E,
  input  [3:0] A,
  input  [3:0] B,
  output [3:0] Q
);

  wire and_1_out, and_2_out, comparator_1_lt, comparator_2_eq, comparator_3_eq, If_B_0_out, If_B_1_out,
       not_1_out, not_2_out, not_3_out, not_4_out, not_5_out, not_6_out, not_7_out, not_8_out, not_9_out,
       not_10_out, not_11_out;
  wire [3:0] adder_1_out, adder_2_out, adder_3_out, Check_q, n4_bit_enabler_1_o, n4_bit_enabler_2_o,
       n4_bit_enabler_3_o, Result_q;

  Hex_Digit_Display hex_digit_display_1 (.value(A));  // open: dp
  Hex_Digit_Display hex_digit_display_2 (.value(B));  // open: dp
  not not_1 (not_1_out, B[0]);
  not not_2 (not_2_out, B[1]);
  not not_3 (not_3_out, B[2]);
  not not_4 (not_4_out, B[3]);
  Comparator_part #(.width(4), .mode("unsigned")) comparator_1 (.a(A), .b(B), .lt(comparator_1_lt));  // open: gt, eq
  and If_B_0 (If_B_0_out, not_1_out, not_2_out, not_3_out, not_4_out);
  not not_5 (not_5_out, B[1]);
  and If_B_1 (If_B_1_out, B[0], not_5_out, not_6_out, not_7_out);
  not not_6 (not_6_out, B[2]);
  not not_7 (not_7_out, B[3]);
  not not_8 (not_8_out, comparator_3_eq);
  not not_9 (not_9_out, comparator_1_lt);
  not not_10 (not_10_out, If_B_0_out);
  not not_11 (not_11_out, If_B_1_out);
  and and_1 (and_1_out, not_8_out, not_9_out, E, not_10_out, not_11_out);
  Register #(.width(4), .trigger("high")) Result (
    .D(n4_bit_enabler_1_o), .en(and_1_out), .Q(Result_q), .clk(and_1_out), .clr(and_2_out));
  Adder #(.width(4)) adder_1 (.a(Result_q), .b(4'b0001), .out(adder_1_out));  // open: cin, cout
  Comparator_part #(.width(4), .mode("unsigned")) comparator_2 (
    .a(n4_bit_enabler_1_o), .b(B), .eq(comparator_2_eq));  // open: gt, lt
  _4_bit_Enabler u_4_bit_enabler_1 (.I(adder_1_out), .O(n4_bit_enabler_1_o), .Enable(and_1_out));
  and and_2 (and_2_out, E, comparator_2_eq);
  Register #(.width(4), .trigger("high")) Check (
    .D(n4_bit_enabler_2_o), .en(and_2_out), .Q(Check_q), .clk(and_2_out));  // open: clr
  Register #(.width(4), .trigger("high")) Count (
    .D(n4_bit_enabler_3_o), .en(and_2_out), .Q(Q), .clk(and_2_out));  // open: clr
  Adder #(.width(4)) adder_2 (.a(Check_q), .b(n4_bit_enabler_1_o), .out(adder_2_out));  // open: cin, cout
  Adder #(.width(4)) adder_3 (.a(Q), .b(4'b0001), .out(adder_3_out));  // open: cin, cout
  _4_bit_Enabler u_4_bit_enabler_2 (.I(adder_2_out), .O(n4_bit_enabler_2_o), .Enable(and_2_out));
  _4_bit_Enabler u_4_bit_enabler_3 (.I(adder_3_out), .O(n4_bit_enabler_3_o), .Enable(and_2_out));
  Comparator_part #(.width(4), .mode("unsigned")) comparator_3 (
    .a(A), .b(Check_q), .eq(comparator_3_eq));  // open: gt, lt
  Hex_Digit_Display hex_digit_display_3 (.value(Q));  // open: dp
endmodule

module Build_3 (
  input  E,
  input  [3:0] A,
  input  [3:0] B,
  input  Clear,
  output [3:0] Q
);

  wire and_1_out, and_2_out, and_3_out, comparator_1_lt, comparator_2_eq, comparator_3_eq, Locker_2_q,
       Locker_q, not_1_out, not_2_out, or_1_out;
  wire [3:0] adder_1_out, compcount_new_1_out_5, n4_bit_enabler_1_o, Result_q, subtractor_1_out,
       subtractor_2_out;

  Hex_Digit_Display hex_digit_display_1 (.value(A));  // open: dp
  Hex_Digit_Display hex_digit_display_2 (.value(B));  // open: dp
  Register #(.width(4), .trigger("high")) Result (
    .D(n4_bit_enabler_1_o), .en(E), .Q(Result_q), .clk(E), .clr(Locker_q));
  D_Flip_Flop #(.trigger("high")) Locker (
    .clk(and_3_out), .D(and_3_out), .Q(Locker_q), .en(and_3_out), .reset(Clear));  // open: Qn, preset
  Subtractor #(.width(4)) subtractor_1 (.a(A), .b(4'b0001), .out(subtractor_1_out));  // open: bin, bout
  Comparator_part #(.width(4), .mode("unsigned")) comparator_1 (.a(A), .b(B), .lt(comparator_1_lt));  // open: gt, eq
  Comparator_part #(.width(4), .mode("unsigned")) comparator_2 (
    .a(Result_q), .b(A), .eq(comparator_2_eq));  // open: gt, lt
  Comparator_part #(.width(4), .mode("unsigned")) comparator_3 (
    .a(Result_q), .b(subtractor_1_out), .eq(comparator_3_eq));  // open: gt, lt
  not not_1 (not_1_out, comparator_1_lt);
  or or_1 (or_1_out, comparator_2_eq, comparator_3_eq);
  LED led_1 (.in(Locker_2_q));
  D_Flip_Flop #(.trigger("high")) Locker_2 (
    .clk(comparator_3_eq), .D(comparator_3_eq), .Q(Locker_2_q), .en(comparator_3_eq));  // open: Qn, preset, reset
  not not_2 (not_2_out, Locker_q);
  and and_1 (and_1_out, E, not_1_out);
  Hex_Digit_Display hex_digit_display_3 (.value(adder_1_out));  // open: dp
  and and_2 (and_2_out, E, not_2_out, not_1_out);
  Adder #(.width(4)) adder_1 (.a(Result_q), .b(B), .out(adder_1_out));  // open: cin, cout
  _4_bit_Enabler u_4_bit_enabler_1 (.I(adder_1_out), .O(n4_bit_enabler_1_o), .Enable(and_2_out));
  and and_3 (and_3_out, and_2_out, or_1_out);
  CompCount_new compcount_new_1 (
    .I(n4_bit_enabler_1_o), .out_5(compcount_new_1_out_5), .Enable_Input(and_1_out),
    .Enable_Output(and_1_out), .Clear(Clear));
  Subtractor #(.width(4)) subtractor_2 (
    .a(compcount_new_1_out_5), .b(4'b0010), .out(subtractor_2_out));  // open: bin, bout
  Hex_Digit_Display hex_digit_display_4 (.value(Q));  // open: dp
  _4_bit_Enabler u_4_bit_enabler_2 (.I(subtractor_2_out), .O(Q), .Enable(E));
endmodule

module _4_bit_Enabler (
  input  [3:0] I,
  input  Enable,
  output [3:0] O
);

  and and_1 (O[0], Enable, I[0]);
  and and_2 (O[1], Enable, I[1]);
  and and_3 (O[2], Enable, I[2]);
  and and_4 (O[3], Enable, I[3]);
endmodule

module Build_2 (
  input  E,
  input  A3,
  input  A2,
  input  A1,
  input  A0,
  input  B3,
  input  B2,
  input  B1,
  input  B0,
  output Q3,
  output Q2,
  output Q1,
  output Q0
);

  wire and_1_out, and_2_out, and_4_out, and_5_out, comparator_1_eq, comparator_2_lt, comparator_3_eq,
       comparator_4_eq, If_B_1_out, Locker_q, not_1_out, not_2_out, not_3_out, not_4_out, not_5_out,
       not_6_out, not_7_out, or_1_out;
  wire [3:0] and_3_out, compcount_new_1_out_5, n4_bit_xselec_1_o, Result_q;

  _4_bit_Xselec u_4_bit_xselec_1 (
    .A({A3, A2, A1, A0}), .A_prime(and_3_out), .O(n4_bit_xselec_1_o), .Selector_Enable(and_2_out));
  Register #(.width(4), .trigger("high")) Result (
    .D(n4_bit_xselec_1_o), .en(not_1_out), .Q(Result_q), .clk(not_1_out));  // open: clr
  not not_1 (not_1_out, Locker_q);
  D_Flip_Flop #(.trigger("high")) Locker (
    .clk(and_1_out), .D(and_1_out), .Q(Locker_q), .en(and_1_out));  // open: Qn, preset, reset
  and and_1 (and_1_out, and_2_out, or_1_out);
  and and_2 (and_2_out, E, not_7_out);
  Comparator_part #(.width(4), .mode("unsigned")) comparator_1 (
    .a(4'b0000), .b(Result_q), .eq(comparator_1_eq));  // open: gt, lt
  or or_1 (or_1_out, comparator_1_eq, and_3_out[0]);
  Comparator_part #(.width(4), .mode("unsigned")) comparator_2 (
    .a({A3, A2, A1, A0}), .b({B3, B2, B1, B0}), .lt(comparator_2_lt));  // open: gt, eq
  Comparator_part #(.width(4), .mode("unsigned")) comparator_3 (
    .a(Result_q), .b(4'b0001), .eq(comparator_3_eq));  // open: gt, lt
  not not_2 (not_2_out, comparator_4_eq);
  Comparator_part #(.width(4), .mode("unsigned")) comparator_4 (
    .a(4'b0001), .b({A3, A2, A1, A0}), .eq(comparator_4_eq));  // open: gt, lt
  not not_3 (not_3_out, B1);
  and If_B_1 (If_B_1_out, B0, not_3_out, not_4_out, not_5_out);
  not not_4 (not_4_out, B2);
  not not_5 (not_5_out, B3);
  not not_6 (not_6_out, comparator_1_eq);
  not not_7 (not_7_out, comparator_2_lt);
  and and_3 (and_3_out[0], comparator_3_eq, not_2_out);
  Subtractor #(.width(4)) subtractor_1 (.a(Result_q), .b({B3, B2, B1, B0}), .out(and_3_out));  // open: bin, bout
  and and_4 (and_4_out, not_6_out, and_2_out);
  CompCount_new compcount_new_1 (
    .I(and_3_out), .out_5(compcount_new_1_out_5), .Enable_Input(not_7_out), .Enable_Output(and_4_out));  // open: Clear
  and and_5 (and_5_out, If_B_1_out, and_2_out);
  _4_bit_Xselec u_4_bit_xselec_2 (
    .A(compcount_new_1_out_5), .A_prime({A3, A2, A1, A0}), .O({Q3, Q2, Q1, Q0}), .Selector_Enable(and_5_out));
  // Pins of 1 and 4 bits meet at and_3_out

  // Notes on the sheet:
  //   If Result = 1
  //   If A != 1
  //   If Result != 0
  //   If A !< B
endmodule

module Build_1 (
  input  E,
  input  A3,
  input  A2,
  input  A1,
  input  A0,
  input  B3,
  input  B2,
  input  B1,
  input  B0,
  output Q3,
  output Q2,
  output Q1,
  output Q0
);

  wire and_1_out, and_2_out, and_4_out, comparator_1_eq, comparator_2_lt, comparator_3_eq, comparator_4_eq,
       Locker_q, not_1_out, not_2_out, not_3_out, not_4_out, or_1_out;
  wire [3:0] and_3_out, n4_bit_xselec_1_o, Result_q;

  Register #(.width(4), .trigger("high")) Result (
    .D(n4_bit_xselec_1_o), .en(not_1_out), .Q(Result_q), .clk(not_1_out));  // open: clr
  _4_bit_Xselec u_4_bit_xselec_1 (
    .A({A3, A2, A1, A0}), .A_prime(and_3_out), .O(n4_bit_xselec_1_o), .Selector_Enable(and_2_out));
  not not_1 (not_1_out, Locker_q);
  D_Flip_Flop #(.trigger("high")) Locker (
    .clk(and_1_out), .D(and_1_out), .Q(Locker_q), .en(and_1_out));  // open: Qn, preset, reset
  and and_1 (and_1_out, and_2_out, or_1_out);
  and and_2 (and_2_out, E, not_3_out);
  Comparator_part #(.width(4), .mode("unsigned")) comparator_1 (
    .a(4'b0000), .b(Result_q), .eq(comparator_1_eq));  // open: gt, lt
  or or_1 (or_1_out, comparator_1_eq, and_3_out[0]);
  Comparator_part #(.width(4), .mode("unsigned")) comparator_2 (
    .a({A3, A2, A1, A0}), .b({B3, B2, B1, B0}), .lt(comparator_2_lt));  // open: gt, eq
  Comparator_part #(.width(4), .mode("unsigned")) comparator_3 (
    .a(and_3_out), .b(4'b0001), .eq(comparator_3_eq));  // open: gt, lt
  Comparator_part #(.width(4), .mode("unsigned")) comparator_4 (
    .a(4'b0001), .b({A3, A2, A1, A0}), .eq(comparator_4_eq));  // open: gt, lt
  not not_2 (not_2_out, comparator_1_eq);
  not not_3 (not_3_out, comparator_2_lt);
  and and_3 (and_3_out[0], comparator_3_eq, not_4_out);
  not not_4 (not_4_out, comparator_4_eq);
  Subtractor #(.width(4)) subtractor_1 (.a(Result_q), .b({B3, B2, B1, B0}), .out(and_3_out));  // open: bin, bout
  and and_4 (and_4_out, not_2_out, and_2_out);
  CompCount_new compcount_new_1 (
    .I(and_3_out), .out_5({Q3, Q2, Q1, Q0}), .Enable_Input(1'b1), .Enable_Output(and_4_out));  // open: Clear
  // Pins of 1 and 4 bits meet at and_3_out
endmodule

module main_new_logic_sub (
  input  E,
  input  [3:0] A,
  input  [3:0] B,
  output [3:0] Q
);

  wire and_1_out, and_2_out, and_4_out, comparator_1_eq, comparator_2_lt, comparator_3_eq, comparator_4_eq,
       Locker_2_q, Locker_q, not_1_out, not_2_out, not_3_out, not_4_out, or_1_out;
  wire [3:0] and_3_out, compcount_new_1_out_5, e_add_1_q, n4_bit_xselec_1_o, Result_q;

  Hex_Digit_Display hex_digit_display_1 (.value(B));  // open: dp
  Hex_Digit_Display hex_digit_display_2 (.value(A));  // open: dp
  _4_bit_Xselec u_4_bit_xselec_1 (.A(A), .A_prime(and_3_out), .O(n4_bit_xselec_1_o), .Selector_Enable(and_2_out));
  Register #(.width(4), .trigger("high")) Result (
    .D(n4_bit_xselec_1_o), .en(not_1_out), .Q(Result_q), .clk(not_1_out));  // open: clr
  not not_1 (not_1_out, Locker_q);
  D_Flip_Flop #(.trigger("high")) Locker (
    .clk(and_1_out), .D(and_1_out), .Q(Locker_q), .en(and_1_out));  // open: Qn, preset, reset
  and and_1 (and_1_out, and_2_out, or_1_out);
  and and_2 (and_2_out, E, not_4_out);
  Comparator_part #(.width(4), .mode("unsigned")) comparator_1 (
    .a(4'b0000), .b(Result_q), .eq(comparator_1_eq));  // open: gt, lt
  or or_1 (or_1_out, comparator_1_eq, and_3_out[0]);
  Comparator_part #(.width(4), .mode("unsigned")) comparator_2 (.a(A), .b(B), .lt(comparator_2_lt));  // open: gt, eq
  Comparator_part #(.width(4), .mode("unsigned")) comparator_3 (
    .a(and_3_out), .b(4'b0001), .eq(comparator_3_eq));  // open: gt, lt
  Comparator_part #(.width(4), .mode("unsigned")) comparator_4 (
    .a(4'b0001), .b(A), .eq(comparator_4_eq));  // open: gt, lt
  not not_2 (not_2_out, comparator_4_eq);
  not not_3 (not_3_out, comparator_1_eq);
  not not_4 (not_4_out, comparator_2_lt);
  and and_3 (and_3_out[0], comparator_3_eq, not_2_out);
  Subtractor #(.width(4)) subtractor_1 (.a(Result_q), .b(B), .out(and_3_out));  // open: bin, bout
  and and_4 (and_4_out, not_3_out, and_2_out);
  D_Flip_Flop #(.trigger("high")) Locker_2 (
    .clk(and_3_out[0]), .D(and_3_out[0]), .Q(Locker_2_q), .en(and_3_out[0]));  // open: Qn, preset, reset
  E_Add e_add_1 (.A(compcount_new_1_out_5), .B(4'b0001), .Enable(Locker_2_q), .Q(e_add_1_q));  // open: Q_unen
  CompCount_new compcount_new_1 (
    .I(and_3_out), .out_5(compcount_new_1_out_5), .Enable_Input(1'b1), .Enable_Output(and_4_out));  // open: Clear
  Hex_Digit_Display hex_digit_display_3 (.value(Q));  // open: dp
  _4_bit_Xselec u_4_bit_xselec_2 (
    .A(compcount_new_1_out_5), .A_prime(e_add_1_q), .O(Q), .Selector_Enable(and_3_out[0]));
  // Pins of 1 and 4 bits meet at and_3_out
endmodule

module _4_bit_Xselec (
  input  Selector_Enable,
  input  [3:0] A,
  input  [3:0] A_prime,
  output [3:0] O
);

  wire and_1_out, and_2_out, and_3_out, and_4_out, and_5_out, and_6_out, and_7_out, and_8_out, d_ff_1_q,
       not_1_out, not_2_out, not_3_out, not_4_out;

  D_Flip_Flop #(.trigger("high")) d_ff_1 (
    .clk(Selector_Enable), .D(Selector_Enable), .Q(d_ff_1_q), .en(Selector_Enable));  // open: Qn, preset, reset
  not not_1 (not_1_out, d_ff_1_q);
  and and_1 (and_1_out, not_1_out, A[0]);
  not not_2 (not_2_out, d_ff_1_q);
  and and_2 (and_2_out, not_2_out, A[1]);
  not not_3 (not_3_out, d_ff_1_q);
  and and_3 (and_3_out, not_3_out, A[2]);
  not not_4 (not_4_out, d_ff_1_q);
  and and_4 (and_4_out, not_4_out, A[3]);
  and and_5 (and_5_out, d_ff_1_q, A_prime[0]);
  and and_6 (and_6_out, d_ff_1_q, A_prime[1]);
  and and_7 (and_7_out, d_ff_1_q, A_prime[2]);
  and and_8 (and_8_out, d_ff_1_q, A_prime[3]);
  or or_1 (O[0], and_1_out, and_5_out);
  or or_2 (O[1], and_2_out, and_6_out);
  or or_3 (O[2], and_3_out, and_7_out);
  or or_4 (O[3], and_4_out, and_8_out);
endmodule

module main_new_logic (
  input  E,
  input  [3:0] A,
  input  [3:0] B,
  output [3:0] Q
);

  wire and_1_out, comparator_1_eq, comparator_1_gt, comparator_1_lt, comparator_2_lt, d_ff_1_q, not_1_out,
       not_2_out, not_3_out, or_1_out;
  wire [3:0] compcount_new_1_out_5, e_add_1_q, e_add_1_q_unen, register_1_q;

  Register #(.width(4), .trigger("high")) register_1 (
    .D(e_add_1_q), .en(not_1_out), .Q(register_1_q), .clk(not_1_out));  // open: clr
  not not_1 (not_1_out, d_ff_1_q);
  Hex_Digit_Display hex_digit_display_1 (.value(A));  // open: dp
  D_Flip_Flop #(.trigger("high")) d_ff_1 (
    .clk(or_1_out), .D(or_1_out), .Q(d_ff_1_q), .en(or_1_out), .reset(not_2_out));  // open: Qn, preset
  not not_2 (not_2_out, E);
  CompCount_new compcount_new_1 (
    .I(register_1_q), .out_5(compcount_new_1_out_5), .Enable_Input(E), .Enable_Output(E));  // open: Clear
  Comparator_part #(.width(4), .mode("unsigned")) comparator_1 (
    .a(A), .b(register_1_q), .gt(comparator_1_gt), .eq(comparator_1_eq), .lt(comparator_1_lt));
  or or_1 (or_1_out, comparator_1_lt, comparator_1_eq);
  Comparator_part #(.width(4), .mode("unsigned")) comparator_2 (.a(A), .b(B), .lt(comparator_2_lt));  // open: gt, eq
  and and_1 (and_1_out, comparator_1_gt, not_3_out, E);
  not not_3 (not_3_out, comparator_2_lt);
  E_Sub e_sub_1 (.A(compcount_new_1_out_5), .B(4'b0010), .Enable(E), .Q_unen(Q));  // open: Q
  Hex_Digit_Display hex_digit_display_2 (.value(e_add_1_q_unen));  // open: dp
  E_Add e_add_1 (.A(register_1_q), .B(B), .Enable(and_1_out), .Q_unen(e_add_1_q_unen), .Q(e_add_1_q));
  Hex_Digit_Display hex_digit_display_3 (.value(Q));  // open: dp
endmodule

// Add
module E_Add (
  input  [3:0] A,
  input  Enable,
  input  [3:0] B,
  output [3:0] Q_unen,
  output [3:0] Q
);

  wire adder_1_cout, adder_2_cout, adder_3_cout;

  Adder #(.width(1)) adder_1 (.a(A[0]), .b(B[0]), .out(Q_unen[0]), .cout(adder_1_cout));  // open: cin
  Adder #(.width(1)) adder_2 (.a(A[1]), .b(B[1]), .out(Q_unen[1]), .cin(adder_1_cout), .cout(adder_2_cout));
  Adder #(.width(1)) adder_3 (.a(A[2]), .b(B[2]), .out(Q_unen[2]), .cin(adder_2_cout), .cout(adder_3_cout));
  Adder #(.width(1)) adder_4 (.a(A[3]), .b(B[3]), .out(Q_unen[3]), .cin(adder_3_cout));  // open: cout
  and and_1 (Q[0], Enable, Q_unen[0]);
  and and_2 (Q[1], Enable, Q_unen[1]);
  and and_3 (Q[2], Enable, Q_unen[2]);
  and and_4 (Q[3], Enable, Q_unen[3]);
endmodule

module CompCount_new (
  input  Enable_Input,
  input  Enable_Output,
  input  [3:0] I,
  input  Clear,
  output [3:0] out_5
);

  wire and_1_out, d_ff_1_q, d_ff_2_q, d_ff_3_q, d_ff_3_qn, d_ff_4_q, d_ff_5_q, d_ff_5_qn, d_ff_6_q,
       d_ff_6_qn, d_ff_7_q, d_ff_7_qn, d_ff_8_q, d_ff_8_qn, or_1_out, xor_1_out, xor_2_out, xor_3_out,
       xor_4_out;

  D_Flip_Flop #(.trigger("high")) d_ff_1 (
    .clk(Enable_Input), .D(I[0]), .Q(d_ff_1_q), .en(xor_1_out), .reset(Clear));  // open: Qn, preset
  xor xor_1 (xor_1_out, I[0], d_ff_1_q);
  D_Flip_Flop #(.trigger("high")) d_ff_2 (
    .clk(Enable_Input), .D(I[1]), .Q(d_ff_2_q), .en(xor_2_out), .reset(Clear));  // open: Qn, preset
  xor xor_2 (xor_2_out, I[1], d_ff_2_q);
  D_Flip_Flop #(.trigger("high")) d_ff_3 (
    .clk(Enable_Input), .D(I[2]), .Q(d_ff_3_q), .Qn(d_ff_3_qn), .en(xor_3_out), .reset(Clear));  // open: preset
  xor xor_3 (xor_3_out, I[2], d_ff_3_q);
  D_Flip_Flop #(.trigger("high")) d_ff_4 (
    .clk(Enable_Input), .D(I[3]), .Q(d_ff_4_q), .en(xor_4_out), .reset(Clear));  // open: Qn, preset
  xor xor_4 (xor_4_out, I[3], d_ff_4_q);
  or or_1 (or_1_out, xor_1_out, xor_2_out, xor_3_out, xor_4_out);
  and and_1 (and_1_out, Enable_Output, or_1_out);
  D_Flip_Flop d_ff_5 (
    .clk(and_1_out), .D(d_ff_5_qn), .Q(d_ff_5_q), .Qn(d_ff_5_qn), .en(Enable_Output), .reset(Clear));  // open: preset
  D_Flip_Flop d_ff_6 (
    .clk(d_ff_5_qn), .D(d_ff_6_qn), .Q(d_ff_6_q), .Qn(d_ff_6_qn), .en(Enable_Output), .reset(Clear));  // open: preset
  D_Flip_Flop d_ff_7 (
    .clk(d_ff_6_qn), .D(d_ff_7_qn), .Q(d_ff_7_q), .Qn(d_ff_7_qn), .en(Enable_Output), .reset(Clear));  // open: preset
  D_Flip_Flop d_ff_8 (
    .clk(d_ff_7_qn), .D(d_ff_8_qn), .Q(d_ff_8_q), .Qn(d_ff_8_qn), .en(Enable_Output), .reset(Clear));  // open: preset
  and and_2 (out_5[0], Enable_Output, d_ff_5_q);
  and and_3 (out_5[1], Enable_Output, d_ff_6_q);
  and and_4 (out_5[2], Enable_Output, d_ff_7_q);
  and and_5 (out_5[3], Enable_Output, d_ff_8_q);
endmodule

module main_unfinished (
  input  Enable,
  input  [3:0] A,
  input  [3:0] B,
  input  Clear
);

  wire comparator_1_output, d_ff_1_q, xor_1_out;
  wire [3:0] e_sub_1_q, e_sub_1_q_unen, n4_bit_out_counter_1_out_3, register_1_q, register_2_q,
       xselector_1_o0;

  Xselector xselector_1 (
    .A0(A[0]), .A1(A[1]), .A2(A[2]), .A3(A[3]), .A0_prime(register_2_q[0]), .A1_prime(register_2_q[1]),
    .A2_prime(register_2_q[2]), .A3_prime(register_2_q[3]), .Selector_Enable(Enable), .O0(xselector_1_o0[0]),
    .O1(xselector_1_o0[1]), .O2(xselector_1_o0[2]), .O3(xselector_1_o0[3]));
  Register #(.width(4), .trigger("high")) register_1 (
    .D(xselector_1_o0), .en(1'b1), .Q(register_1_q), .clk(1'b1), .clr(Clear));
  Comparator comparator_1 (
    .A0(register_1_q[0]), .A1(register_1_q[1]), .A2(register_1_q[2]), .A3(register_1_q[3]), .B0(B[0]),
    .B1(B[1]), .B2(B[2]), .B3(B[3]), .Enable_Output(Enable), .Output(comparator_1_output));
  D_Flip_Flop #(.trigger("high")) d_ff_1 (
    .clk(Enable), .D(comparator_1_output), .Q(d_ff_1_q), .en(xor_1_out));  // open: Qn, preset, reset
  xor xor_1 (xor_1_out, comparator_1_output, d_ff_1_q);
  Hex_Digit_Display hex_digit_display_1 (.value(e_sub_1_q_unen));  // open: dp
  E_Sub e_sub_1 (.A(register_1_q), .B(B), .Enable(xor_1_out), .Q_unen(e_sub_1_q_unen), .Q(e_sub_1_q));
  Hex_Digit_Display hex_digit_display_2 (.value(n4_bit_out_counter_1_out_3));  // open: dp
  _4_bit_out_Counter u_4_bit_out_counter_1 (.D(xor_1_out), .Clear(Clear), .out_3(n4_bit_out_counter_1_out_3));
  Register #(.width(4), .trigger("high")) register_2 (
    .D(e_sub_1_q), .en(xor_1_out), .Q(register_2_q), .clk(xor_1_out), .clr(Clear));
  Hex_Digit_Display hex_digit_display_3 (.value(register_2_q));  // open: dp
endmodule

module _4_bit_out_Counter (
  input  D,
  input  Clear,
  output [3:0] out_3
);

  wire d_ff_1_qn, d_ff_2_qn, d_ff_3_qn, d_ff_4_qn, undriven;

  D_Flip_Flop d_ff_1 (
    .clk(D), .D(d_ff_1_qn), .Q(out_3[0]), .Qn(d_ff_1_qn), .en(undriven), .reset(Clear));  // open: preset
  D_Flip_Flop d_ff_2 (
    .clk(d_ff_1_qn), .D(d_ff_2_qn), .Q(out_3[1]), .Qn(d_ff_2_qn), .en(undriven), .reset(Clear));  // open: preset
  D_Flip_Flop d_ff_3 (
    .clk(d_ff_2_qn), .D(d_ff_3_qn), .Q(out_3[2]), .Qn(d_ff_3_qn), .en(undriven), .reset(Clear));  // open: preset
  D_Flip_Flop d_ff_4 (
    .clk(d_ff_3_qn), .D(d_ff_4_qn), .Q(out_3[3]), .Qn(d_ff_4_qn), .en(undriven), .reset(Clear));  // open: preset
endmodule

module Counter (
  input  D,
  input  Clear,
  output Q0,
  output Q1,
  output Q2,
  output Q3
);

  wire d_ff_1_qn, d_ff_2_qn, d_ff_3_qn, d_ff_4_qn, undriven;

  D_Flip_Flop d_ff_1 (.clk(D), .D(d_ff_1_qn), .Q(Q0), .Qn(d_ff_1_qn), .en(undriven), .reset(Clear));  // open: preset
  D_Flip_Flop d_ff_2 (
    .clk(d_ff_1_qn), .D(d_ff_2_qn), .Q(Q1), .Qn(d_ff_2_qn), .en(undriven), .reset(Clear));  // open: preset
  D_Flip_Flop d_ff_3 (
    .clk(d_ff_2_qn), .D(d_ff_3_qn), .Q(Q2), .Qn(d_ff_3_qn), .en(undriven), .reset(Clear));  // open: preset
  D_Flip_Flop d_ff_4 (
    .clk(d_ff_3_qn), .D(d_ff_4_qn), .Q(Q3), .Qn(d_ff_4_qn), .en(undriven), .reset(Clear));  // open: preset
endmodule

// Sub
module E_Sub (
  input  [3:0] A,
  input  Enable,
  input  [3:0] B,
  output [3:0] Q_unen,
  output [3:0] Q
);

  wire adder_1_cout, adder_2_cout, adder_3_cout, not_1_out, not_2_out, not_3_out, not_4_out;

  not not_1 (not_1_out, B[0]);
  not not_2 (not_2_out, B[1]);
  not not_3 (not_3_out, B[2]);
  not not_4 (not_4_out, B[3]);
  Adder #(.width(1)) adder_1 (.a(A[0]), .b(not_1_out), .out(Q_unen[0]), .cin(1'b1), .cout(adder_1_cout));
  Adder #(.width(1)) adder_2 (.a(A[1]), .b(not_2_out), .out(Q_unen[1]), .cin(adder_1_cout), .cout(adder_2_cout));
  Adder #(.width(1)) adder_3 (.a(A[2]), .b(not_3_out), .out(Q_unen[2]), .cin(adder_2_cout), .cout(adder_3_cout));
  Adder #(.width(1)) adder_4 (.a(A[3]), .b(not_4_out), .out(Q_unen[3]), .cin(adder_3_cout));  // open: cout
  and and_1 (Q[0], Enable, Q_unen[0]);
  and and_2 (Q[1], Enable, Q_unen[1]);
  and and_3 (Q[2], Enable, Q_unen[2]);
  and and_4 (Q[3], Enable, Q_unen[3]);
endmodule

module main_old (
  input  A0,
  input  A1,
  input  A2,
  input  A3,
  input  B0,
  input  B1,
  input  in_7,
  input  B2,
  input  B3,
  input  Clear,
  output Q0,
  output Q1,
  output Q2,
  output Q3
);

  wire comparator_1_output, compcounter_eio_1_io0, compcounter_eio_1_io1, compcounter_eio_1_io2,
       compcounter_eio_1_io3, d_ff_1_q, enable_subtractor_1_o0, enable_subtractor_1_o1,
       enable_subtractor_1_o2, enable_subtractor_1_o3, xor_1_out, xselector_1_o0, xselector_1_o1,
       xselector_1_o2, xselector_1_o3;

  Xselector xselector_1 (
    .A0(A0), .A1(A1), .A2(A2), .A3(A3), .A0_prime(enable_subtractor_1_o0), .A1_prime(enable_subtractor_1_o1),
    .A2_prime(enable_subtractor_1_o2), .A3_prime(enable_subtractor_1_o3), .Selector_Enable(xor_1_out),
    .O0(xselector_1_o0), .O1(xselector_1_o1), .O2(xselector_1_o2), .O3(xselector_1_o3));
  CompCounter_EIO compcounter_eio_1 (
    .I0(xselector_1_o0), .I1(xselector_1_o1), .I2(xselector_1_o2), .I3(xselector_1_o3), .Enable_Input(1'b1),
    .Enable_Output(in_7), .Clear(Clear), .Q0(Q0), .Q1(Q1), .Q2(Q2), .Q3(Q3), .Io0(compcounter_eio_1_io0),
    .Io1(compcounter_eio_1_io1), .Io2(compcounter_eio_1_io2), .Io3(compcounter_eio_1_io3));
  Comparator comparator_1 (
    .A0(compcounter_eio_1_io0), .A1(compcounter_eio_1_io1), .A2(compcounter_eio_1_io2),
    .A3(compcounter_eio_1_io3), .B0(B0), .B1(B1), .B2(B2), .B3(B3), .Enable_Output(in_7),
    .Output(comparator_1_output));
  Enable_Subtractor enable_subtractor_1 (
    .A0(compcounter_eio_1_io0), .B0(B0), .A1(compcounter_eio_1_io1), .B1(B1), .A2(compcounter_eio_1_io2),
    .B2(B2), .A3(compcounter_eio_1_io3), .B3(B3), .Enable(xor_1_out), .O0(enable_subtractor_1_o0),
    .O1(enable_subtractor_1_o1), .O2(enable_subtractor_1_o2), .O3(enable_subtractor_1_o3));
  D_Flip_Flop #(.trigger("high")) d_ff_1 (
    .clk(1'b1), .D(comparator_1_output), .Q(d_ff_1_q), .en(xor_1_out));  // open: Qn, preset, reset
  xor xor_1 (xor_1_out, comparator_1_output, d_ff_1_q);
endmodule

module main_Showing_old (
  input  Enable_Output,
  input  A0,
  input  A1,
  input  A2,
  input  A3,
  input  Clear,
  input  B0,
  input  B1,
  input  B2,
  input  Clear_2,
  input  B3,
  output Q0,
  output Q1,
  output Q2,
  output Q3
);

  wire adder_1_cout, adder_1_out, adder_2_cout, adder_2_out, adder_3_cout, adder_3_out, adder_4_out,
       and_1_out, and_2_out, and_3_out, and_4_out, and_5_out, and_6_out, and_7_out, and_8_out, and_9_out,
       and_10_out, and_11_out, and_12_out, and_13_out, and_18_out, and_19_out, and_20_out, and_21_out,
       and_22_out, d_ff_1_q, d_ff_2_q, d_ff_3_q, d_ff_4_q, d_ff_4_qn, d_ff_5_q, d_ff_6_q, d_ff_6_qn,
       d_ff_7_q, d_ff_7_qn, d_ff_8_q, d_ff_8_qn, d_ff_9_q, d_ff_9_qn, d_ff_10_q, d_ff_11_q, d_ff_11_qn,
       d_ff_12_q, d_ff_12_qn, d_ff_13_q, d_ff_14_q, n1_bit_magnitude_comp_1_a_b, n1_bit_magnitude_comp_2_a_b,
       n1_bit_magnitude_comp_2_a_b_2, n1_bit_magnitude_comp_3_a_b, n1_bit_magnitude_comp_3_a_b_2,
       n1_bit_magnitude_comp_4_a_b, n1_bit_magnitude_comp_4_a_b_2, not_1_out, not_2_out, not_3_out,
       not_4_out, not_5_out, not_6_out, not_7_out, not_8_out, not_9_out, not_10_out, or_1_out, or_2_out,
       or_3_out, or_4_out, or_5_out, or_6_out, xor_1_out, xor_2_out, xor_3_out, xor_4_out, xor_5_out;

  D_Flip_Flop #(.trigger("high")) d_ff_1 (
    .clk(Enable_Output), .D(Enable_Output), .Q(d_ff_1_q), .en(Enable_Output));  // open: Qn, preset, reset
  not not_1 (not_1_out, d_ff_1_q);
  and and_1 (and_1_out, not_1_out, A0);
  not not_2 (not_2_out, d_ff_1_q);
  and and_2 (and_2_out, not_2_out, A1);
  not not_3 (not_3_out, d_ff_1_q);
  and and_3 (and_3_out, not_3_out, A2);
  not not_4 (not_4_out, d_ff_1_q);
  and and_4 (and_4_out, not_4_out, A3);
  and and_5 (and_5_out, d_ff_1_q, and_18_out);
  and and_6 (and_6_out, d_ff_1_q, and_19_out);
  and and_7 (and_7_out, d_ff_1_q, and_20_out);
  and and_8 (and_8_out, d_ff_1_q, and_21_out);
  or or_1 (or_1_out, and_1_out, and_5_out);
  or or_2 (or_2_out, and_2_out, and_6_out);
  or or_3 (or_3_out, and_3_out, and_7_out);
  or or_4 (or_4_out, and_4_out, and_8_out);
  D_Flip_Flop #(.trigger("high")) d_ff_2 (
    .clk(1'b1), .D(or_1_out), .Q(d_ff_2_q), .en(xor_1_out), .reset(Clear));  // open: Qn, preset
  xor xor_1 (xor_1_out, or_1_out, d_ff_2_q);
  D_Flip_Flop #(.trigger("high")) d_ff_3 (
    .clk(1'b1), .D(or_2_out), .Q(d_ff_3_q), .en(xor_2_out), .reset(Clear));  // open: Qn, preset
  xor xor_2 (xor_2_out, or_2_out, d_ff_3_q);
  D_Flip_Flop #(.trigger("high")) d_ff_4 (
    .clk(1'b1), .D(or_3_out), .Q(d_ff_4_q), .Qn(d_ff_4_qn), .en(xor_3_out), .reset(Clear));  // open: preset
  xor xor_3 (xor_3_out, or_3_out, d_ff_4_q);
  D_Flip_Flop #(.trigger("high")) d_ff_5 (
    .clk(1'b1), .D(or_4_out), .Q(d_ff_5_q), .en(xor_4_out), .reset(Clear));  // open: Qn, preset
  xor xor_4 (xor_4_out, or_4_out, d_ff_5_q);
  _1_bit_Magnitude_Comp u_1_bit_magnitude_comp_1 (
    .A(or_1_out), .B(B0), .A_B(n1_bit_magnitude_comp_1_a_b));  // open: A_B_2, A_B_3
  _1_bit_Magnitude_Comp u_1_bit_magnitude_comp_2 (
    .A(or_2_out), .B(B1), .A_B(n1_bit_magnitude_comp_2_a_b), .A_B_2(n1_bit_magnitude_comp_2_a_b_2));  // open: A_B_3
  _1_bit_Magnitude_Comp u_1_bit_magnitude_comp_3 (
    .A(or_3_out), .B(B2), .A_B(n1_bit_magnitude_comp_3_a_b), .A_B_2(n1_bit_magnitude_comp_3_a_b_2));  // open: A_B_3
  _1_bit_Magnitude_Comp u_1_bit_magnitude_comp_4 (
    .A(or_4_out), .B(B3), .A_B(n1_bit_magnitude_comp_4_a_b), .A_B_2(n1_bit_magnitude_comp_4_a_b_2));  // open: A_B_3
  and and_9 (and_9_out, n1_bit_magnitude_comp_2_a_b, n1_bit_magnitude_comp_3_a_b_2, n1_bit_magnitude_comp_4_a_b_2);
  and and_10 (and_10_out, n1_bit_magnitude_comp_3_a_b, n1_bit_magnitude_comp_4_a_b_2);
  or or_5 (or_5_out, xor_1_out, xor_2_out, xor_3_out, xor_4_out);
  and and_11 (and_11_out, n1_bit_magnitude_comp_1_a_b, n1_bit_magnitude_comp_2_a_b_2, n1_bit_magnitude_comp_3_a_b_2, n1_bit_magnitude_comp_4_a_b_2);
  and and_12 (and_12_out, Enable_Output, or_5_out);
  not not_5 (not_5_out, or_6_out);
  or or_6 (or_6_out, and_11_out, and_9_out, and_10_out, n1_bit_magnitude_comp_4_a_b);
  D_Flip_Flop d_ff_6 (
    .clk(and_12_out), .D(d_ff_6_qn), .Q(d_ff_6_q), .Qn(d_ff_6_qn), .en(Enable_Output), .reset(Clear));  // open: preset
  D_Flip_Flop d_ff_7 (
    .clk(d_ff_6_qn), .D(d_ff_7_qn), .Q(d_ff_7_q), .Qn(d_ff_7_qn), .en(Enable_Output), .reset(Clear));  // open: preset
  D_Flip_Flop d_ff_8 (
    .clk(d_ff_7_qn), .D(d_ff_8_qn), .Q(d_ff_8_q), .Qn(d_ff_8_qn), .en(Enable_Output), .reset(Clear));  // open: preset
  D_Flip_Flop d_ff_9 (
    .clk(d_ff_8_qn), .D(d_ff_9_qn), .Q(d_ff_9_q), .Qn(d_ff_9_qn), .en(Enable_Output), .reset(Clear));  // open: preset
  and and_13 (and_13_out, Enable_Output, not_5_out);
  D_Flip_Flop #(.trigger("high")) d_ff_10 (
    .clk(Enable_Output), .D(and_13_out), .Q(d_ff_10_q), .en(xor_5_out));  // open: Qn, preset, reset
  xor xor_5 (xor_5_out, and_13_out, d_ff_10_q);
  not not_6 (not_6_out, B0);
  not not_7 (not_7_out, B1);
  not not_8 (not_8_out, B2);
  not not_9 (not_9_out, B3);
  Adder #(.width(1)) adder_1 (.a(or_4_out), .b(not_6_out), .out(adder_1_out), .cin(1'b1), .cout(adder_1_cout));
  Adder #(.width(1)) adder_2 (.a(or_3_out), .b(not_7_out), .out(adder_2_out), .cin(adder_1_cout), .cout(adder_2_cout));
  Adder #(.width(1)) adder_3 (.a(or_2_out), .b(not_8_out), .out(adder_3_out), .cin(adder_2_cout), .cout(adder_3_cout));
  Adder #(.width(1)) adder_4 (.a(or_1_out), .b(not_9_out), .out(adder_4_out), .cin(adder_3_cout));  // open: cout
  and and_14 (Q0, Enable_Output, d_ff_6_q);
  and and_15 (Q1, Enable_Output, d_ff_7_q);
  and and_16 (Q2, Enable_Output, d_ff_8_q);
  and and_17 (Q3, Enable_Output, d_ff_9_q);
  D_Flip_Flop d_ff_11 (
    .clk(xor_5_out), .D(d_ff_11_qn), .Q(d_ff_11_q), .Qn(d_ff_11_qn), .en(Enable_Output), .reset(Clear_2));  // open: preset
  D_Flip_Flop d_ff_12 (
    .clk(d_ff_11_qn), .D(d_ff_12_qn), .Q(d_ff_12_q), .Qn(d_ff_12_qn), .en(Enable_Output), .reset(Clear_2));  // open: preset
  and and_18 (and_18_out, and_22_out, adder_1_out);
  and and_19 (and_19_out, and_22_out, adder_2_out);
  and and_20 (and_20_out, and_22_out, adder_3_out);
  and and_21 (and_21_out, and_22_out, adder_4_out);
  D_Flip_Flop #(.trigger("high")) d_ff_13 (
    .clk(d_ff_11_q), .D(d_ff_11_q), .Q(d_ff_13_q), .en(d_ff_11_q), .reset(Clear_2));  // open: Qn, preset
  D_Flip_Flop #(.trigger("high")) d_ff_14 (
    .clk(d_ff_12_q), .D(d_ff_12_q), .Q(d_ff_14_q), .en(d_ff_12_q), .reset(Clear_2));  // open: Qn, preset
  not not_10 (not_10_out, d_ff_14_q);
  and and_22 (and_22_out, d_ff_13_q, not_10_out);
endmodule

module Comparator (
  input  Enable_Output,
  input  A0,
  input  A1,
  input  A2,
  input  A3,
  input  B0,
  input  B1,
  input  B2,
  input  B3,
  output Output
);

  wire and_1_out, and_2_out, and_3_out, n1_bit_magnitude_comp_1_a_b, n1_bit_magnitude_comp_2_a_b,
       n1_bit_magnitude_comp_2_a_b_2, n1_bit_magnitude_comp_3_a_b, n1_bit_magnitude_comp_3_a_b_2,
       n1_bit_magnitude_comp_4_a_b, n1_bit_magnitude_comp_4_a_b_2, not_1_out, or_1_out;

  _1_bit_Magnitude_Comp u_1_bit_magnitude_comp_1 (
    .A(A0), .B(B0), .A_B(n1_bit_magnitude_comp_1_a_b));  // open: A_B_2, A_B_3
  _1_bit_Magnitude_Comp u_1_bit_magnitude_comp_2 (
    .A(A1), .B(B1), .A_B(n1_bit_magnitude_comp_2_a_b), .A_B_2(n1_bit_magnitude_comp_2_a_b_2));  // open: A_B_3
  _1_bit_Magnitude_Comp u_1_bit_magnitude_comp_3 (
    .A(A2), .B(B2), .A_B(n1_bit_magnitude_comp_3_a_b), .A_B_2(n1_bit_magnitude_comp_3_a_b_2));  // open: A_B_3
  _1_bit_Magnitude_Comp u_1_bit_magnitude_comp_4 (
    .A(A3), .B(B3), .A_B(n1_bit_magnitude_comp_4_a_b), .A_B_2(n1_bit_magnitude_comp_4_a_b_2));  // open: A_B_3
  and and_1 (and_1_out, n1_bit_magnitude_comp_1_a_b, n1_bit_magnitude_comp_2_a_b_2, n1_bit_magnitude_comp_3_a_b_2, n1_bit_magnitude_comp_4_a_b_2);
  and and_2 (and_2_out, n1_bit_magnitude_comp_2_a_b, n1_bit_magnitude_comp_3_a_b_2, n1_bit_magnitude_comp_4_a_b_2);
  and and_3 (and_3_out, n1_bit_magnitude_comp_3_a_b, n1_bit_magnitude_comp_4_a_b_2);
  or or_1 (or_1_out, and_1_out, and_2_out, and_3_out, n1_bit_magnitude_comp_4_a_b);
  not not_1 (not_1_out, or_1_out);
  and and_4 (Output, Enable_Output, not_1_out);
endmodule

// ComCount
module CompCounter_EI (
  input  Enable,
  input  I0,
  input  I1,
  input  I2,
  input  I3,
  input  Clear,
  output Q0,
  output Q1,
  output Q2,
  output Q3,
  output Io0,
  output Io1,
  output Io2,
  output Io3
);

  wire d_ff_1_q, d_ff_2_q, d_ff_3_q, d_ff_3_qn, d_ff_4_q, d_ff_5_qn, d_ff_6_qn, d_ff_7_qn, d_ff_8_qn,
       or_1_out, xor_1_out, xor_2_out, xor_3_out, xor_4_out;

  and and_1 (Io0, Enable, I0);
  and and_2 (Io1, Enable, I1);
  and and_3 (Io2, Enable, I2);
  and and_4 (Io3, Enable, I3);
  D_Flip_Flop #(.trigger("high")) d_ff_1 (
    .clk(Enable), .D(Io0), .Q(d_ff_1_q), .en(xor_1_out), .reset(Clear));  // open: Qn, preset
  xor xor_1 (xor_1_out, Io0, d_ff_1_q);
  D_Flip_Flop #(.trigger("high")) d_ff_2 (
    .clk(Enable), .D(Io1), .Q(d_ff_2_q), .en(xor_2_out), .reset(Clear));  // open: Qn, preset
  xor xor_2 (xor_2_out, Io1, d_ff_2_q);
  D_Flip_Flop #(.trigger("high")) d_ff_3 (
    .clk(Enable), .D(Io2), .Q(d_ff_3_q), .Qn(d_ff_3_qn), .en(xor_3_out), .reset(Clear));  // open: preset
  xor xor_3 (xor_3_out, Io2, d_ff_3_q);
  D_Flip_Flop #(.trigger("high")) d_ff_4 (
    .clk(Enable), .D(Io3), .Q(d_ff_4_q), .en(xor_4_out), .reset(Clear));  // open: Qn, preset
  xor xor_4 (xor_4_out, Io3, d_ff_4_q);
  or or_1 (or_1_out, xor_1_out, xor_2_out, xor_3_out, xor_4_out);
  D_Flip_Flop d_ff_5 (
    .clk(or_1_out), .D(d_ff_5_qn), .Q(Q0), .Qn(d_ff_5_qn), .en(Enable), .reset(Clear));  // open: preset
  D_Flip_Flop d_ff_6 (
    .clk(d_ff_5_qn), .D(d_ff_6_qn), .Q(Q1), .Qn(d_ff_6_qn), .en(Enable), .reset(Clear));  // open: preset
  D_Flip_Flop d_ff_7 (
    .clk(d_ff_6_qn), .D(d_ff_7_qn), .Q(Q2), .Qn(d_ff_7_qn), .en(Enable), .reset(Clear));  // open: preset
  D_Flip_Flop d_ff_8 (
    .clk(d_ff_7_qn), .D(d_ff_8_qn), .Q(Q3), .Qn(d_ff_8_qn), .en(Enable), .reset(Clear));  // open: preset
endmodule

module CompCounter_EIO (
  input  Enable_Input,
  input  Enable_Output,
  input  I0,
  input  I1,
  input  I2,
  input  I3,
  input  Clear,
  output Q0,
  output Q1,
  output Q2,
  output Q3,
  output Io0,
  output Io1,
  output Io2,
  output Io3
);

  wire and_1_out, d_ff_1_q, d_ff_2_q, d_ff_3_q, d_ff_3_qn, d_ff_4_q, d_ff_5_q, d_ff_5_qn, d_ff_6_q,
       d_ff_6_qn, d_ff_7_q, d_ff_7_qn, d_ff_8_q, d_ff_8_qn, or_1_out, xor_1_out, xor_2_out, xor_3_out,
       xor_4_out;

  D_Flip_Flop #(.trigger("high")) d_ff_1 (
    .clk(Enable_Input), .D(I0), .Q(d_ff_1_q), .en(xor_1_out), .reset(Clear));  // open: Qn, preset
  xor xor_1 (xor_1_out, I0, d_ff_1_q);
  D_Flip_Flop #(.trigger("high")) d_ff_2 (
    .clk(Enable_Input), .D(I1), .Q(d_ff_2_q), .en(xor_2_out), .reset(Clear));  // open: Qn, preset
  xor xor_2 (xor_2_out, I1, d_ff_2_q);
  D_Flip_Flop #(.trigger("high")) d_ff_3 (
    .clk(Enable_Input), .D(I2), .Q(d_ff_3_q), .Qn(d_ff_3_qn), .en(xor_3_out), .reset(Clear));  // open: preset
  xor xor_3 (xor_3_out, I2, d_ff_3_q);
  D_Flip_Flop #(.trigger("high")) d_ff_4 (
    .clk(Enable_Input), .D(I3), .Q(d_ff_4_q), .en(xor_4_out), .reset(Clear));  // open: Qn, preset
  xor xor_4 (xor_4_out, I3, d_ff_4_q);
  or or_1 (or_1_out, xor_1_out, xor_2_out, xor_3_out, xor_4_out);
  and and_1 (and_1_out, Enable_Output, or_1_out);
  D_Flip_Flop d_ff_5 (
    .clk(and_1_out), .D(d_ff_5_qn), .Q(d_ff_5_q), .Qn(d_ff_5_qn), .en(Enable_Output), .reset(Clear));  // open: preset
  D_Flip_Flop d_ff_6 (
    .clk(d_ff_5_qn), .D(d_ff_6_qn), .Q(d_ff_6_q), .Qn(d_ff_6_qn), .en(Enable_Output), .reset(Clear));  // open: preset
  D_Flip_Flop d_ff_7 (
    .clk(d_ff_6_qn), .D(d_ff_7_qn), .Q(d_ff_7_q), .Qn(d_ff_7_qn), .en(Enable_Output), .reset(Clear));  // open: preset
  D_Flip_Flop d_ff_8 (
    .clk(d_ff_7_qn), .D(d_ff_8_qn), .Q(d_ff_8_q), .Qn(d_ff_8_qn), .en(Enable_Output), .reset(Clear));  // open: preset
  and and_2 (Q0, Enable_Output, d_ff_5_q);
  and and_3 (Q1, Enable_Output, d_ff_6_q);
  and and_4 (Q2, Enable_Output, d_ff_7_q);
  and and_5 (Q3, Enable_Output, d_ff_8_q);

  assign Io0 = I0;
  assign Io1 = I1;
  assign Io2 = I2;
  assign Io3 = I3;
endmodule

module _1_bit_Magnitude_Comp (
  input  A,
  input  B,
  output A_B,
  output A_B_2,
  output A_B_3
);

  wire not_1_out, not_2_out;

  not not_1 (not_1_out, A);
  not not_2 (not_2_out, B);
  and and_1 (A_B, not_1_out, B);
  and and_2 (A_B_3, A, not_2_out);
  nor nor_1 (A_B_2, A_B, A_B_3);
endmodule

// Subtractor
module Enable_Subtractor (
  input  Enable,
  input  A0,
  input  B0,
  input  A1,
  input  B1,
  input  A2,
  input  B2,
  input  A3,
  input  B3,
  output O0,
  output O1,
  output O2,
  output O3
);

  wire adder_1_cout, adder_1_out, adder_2_cout, adder_2_out, adder_3_cout, adder_3_out, adder_4_out,
       not_1_out, not_2_out, not_3_out, not_4_out;

  not not_1 (not_1_out, B0);
  not not_2 (not_2_out, B1);
  not not_3 (not_3_out, B2);
  not not_4 (not_4_out, B3);
  Adder #(.width(1)) adder_1 (.a(A0), .b(not_1_out), .out(adder_1_out), .cin(1'b1), .cout(adder_1_cout));
  Adder #(.width(1)) adder_2 (.a(A1), .b(not_2_out), .out(adder_2_out), .cin(adder_1_cout), .cout(adder_2_cout));
  Adder #(.width(1)) adder_3 (.a(A2), .b(not_3_out), .out(adder_3_out), .cin(adder_2_cout), .cout(adder_3_cout));
  Adder #(.width(1)) adder_4 (.a(A3), .b(not_4_out), .out(adder_4_out), .cin(adder_3_cout));  // open: cout
  and and_1 (O0, Enable, adder_1_out);
  and and_2 (O1, Enable, adder_2_out);
  and and_3 (O2, Enable, adder_3_out);
  and and_4 (O3, Enable, adder_4_out);
endmodule

// Xselec
module Xselector (
  input  Selector_Enable,
  input  A0,
  input  A1,
  input  A2,
  input  A3,
  input  A0_prime,
  input  A1_prime,
  input  A2_prime,
  input  A3_prime,
  output O0,
  output O1,
  output O2,
  output O3
);

  wire and_1_out, and_2_out, and_3_out, and_4_out, and_5_out, and_6_out, and_7_out, and_8_out, d_ff_1_q,
       not_1_out, not_2_out, not_3_out, not_4_out;

  D_Flip_Flop #(.trigger("high")) d_ff_1 (
    .clk(Selector_Enable), .D(Selector_Enable), .Q(d_ff_1_q), .en(Selector_Enable));  // open: Qn, preset, reset
  not not_1 (not_1_out, d_ff_1_q);
  not not_2 (not_2_out, d_ff_1_q);
  not not_3 (not_3_out, d_ff_1_q);
  not not_4 (not_4_out, d_ff_1_q);
  and and_1 (and_1_out, not_1_out, A0);
  and and_2 (and_2_out, not_2_out, A1);
  and and_3 (and_3_out, not_3_out, A2);
  and and_4 (and_4_out, not_4_out, A3);
  and and_5 (and_5_out, d_ff_1_q, A0_prime);
  and and_6 (and_6_out, d_ff_1_q, A1_prime);
  and and_7 (and_7_out, d_ff_1_q, A2_prime);
  and and_8 (and_8_out, d_ff_1_q, A3_prime);
  or or_1 (O0, and_1_out, and_5_out);
  or or_2 (O1, and_2_out, and_6_out);
  or or_3 (O2, and_3_out, and_7_out);
  or or_4 (O3, and_4_out, and_8_out);
endmodule

// AK
module AK_Locker (
  input  Enable,
  input  AK,
  input  Clear,
  output Allow
);

  wire d_ff_1_q, d_ff_2_q, d_ff_2_qn, d_ff_3_q, d_ff_3_qn, d_ff_4_q, d_ff_5_q, not_1_out, xor_1_out;

  D_Flip_Flop #(.trigger("high")) d_ff_1 (
    .clk(Enable), .D(AK), .Q(d_ff_1_q), .en(xor_1_out));  // open: Qn, preset, reset
  xor xor_1 (xor_1_out, AK, d_ff_1_q);
  D_Flip_Flop d_ff_2 (
    .clk(xor_1_out), .D(d_ff_2_qn), .Q(d_ff_2_q), .Qn(d_ff_2_qn), .en(Enable), .reset(Clear));  // open: preset
  D_Flip_Flop d_ff_3 (
    .clk(d_ff_2_qn), .D(d_ff_3_qn), .Q(d_ff_3_q), .Qn(d_ff_3_qn), .en(Enable), .reset(Clear));  // open: preset
  D_Flip_Flop #(.trigger("high")) d_ff_4 (
    .clk(d_ff_2_q), .D(d_ff_2_q), .Q(d_ff_4_q), .en(d_ff_2_q), .reset(Clear));  // open: Qn, preset
  D_Flip_Flop #(.trigger("high")) d_ff_5 (
    .clk(d_ff_3_q), .D(d_ff_3_q), .Q(d_ff_5_q), .en(d_ff_3_q), .reset(Clear));  // open: Qn, preset
  and and_1 (Allow, d_ff_4_q, not_1_out);
  not not_1 (not_1_out, d_ff_5_q);
endmodule

module Test (
  input  Enable_Input,
  input  Enable_Loop,
  input  [3:0] Increment,
  input  Clear,
  output [3:0] Output,
  output out_6
);

  wire [3:0] adder_1_out, n4_bit_enabler_1_o;

  Register #(.width(4), .trigger("high")) register_1 (
    .D(n4_bit_enabler_1_o), .Q(Output), .clk(Enable_Input), .clr(Clear));  // open: en
  Adder #(.width(4)) adder_1 (.a(Output), .b(Increment), .out(adder_1_out), .cout(out_6));  // open: cin
  _4_bit_Enabler u_4_bit_enabler_1 (.I(adder_1_out), .O(n4_bit_enabler_1_o), .Enable(Enable_Loop));
endmodule
