// Logisim project Divider_old.circ as structural Verilog: 9 circuits, main circuit main
module main (
  input  d,
  input  c,
  input  b,
  input  a,
  output q0,
  output q1
);

  wire and_1_out, and_2_out, and_3_out, and_4_out, and_5_out, and_6_out, not_1_out, not_2_out, not_3_out,
       not_4_out, not_5_out, not_6_out, not_7_out, undriven;

  not not_1 (not_1_out, b);
  not not_2 (not_2_out, a);
  not not_3 (not_3_out, c);
  not not_4 (not_4_out, b);
  not not_5 (not_5_out, b);
  not not_6 (not_6_out, a);
  not not_7 (not_7_out, b);
  and and_1 (and_1_out, not_1_out, c, undriven);
  and and_2 (and_2_out, not_2_out, b, not_3_out);
  and and_3 (and_3_out, a, not_4_out, undriven);
  and and_4 (and_4_out, a, not_5_out, c);
  and and_5 (and_5_out, not_6_out, b, c);
  and and_6 (and_6_out, a, not_7_out);
  or or_1 (q0, and_1_out, and_2_out, and_3_out, and_4_out);
  or or_2 (q1, and_5_out, and_6_out);
endmodule

module _2_bit_divider (
  input  A2,
  input  A1,
  input  B2,
  input  B1,
  output Q1,
  output Q2
);

  wire and_1_out, and_2_out, and_3_out, and_4_out, and_5_out, and_6_out, not_1_out, not_2_out, not_3_out,
       not_4_out, not_5_out, not_6_out, not_7_out;

  not not_1 (not_1_out, B1);
  not not_2 (not_2_out, B2);
  not not_3 (not_3_out, B2);
  not not_4 (not_4_out, B1);
  not not_5 (not_5_out, B2);
  not not_6 (not_6_out, B1);
  not not_7 (not_7_out, B2);
  and and_1 (and_1_out, not_1_out, not_2_out);
  and and_2 (and_2_out, not_3_out, A1);
  and and_3 (and_3_out, not_4_out, A2);
  and and_4 (and_4_out, A1, A2);
  and and_5 (and_5_out, not_5_out, not_6_out);
  and and_6 (and_6_out, not_7_out, A2);
  or or_1 (Q1, and_1_out, and_2_out, and_3_out, and_4_out);
  or or_2 (Q2, and_5_out, and_6_out);

  // Notes on the sheet:
  //   A2: 0 0 1 1 0 0 1 1 0 0 1 1 0 0 1 1
  //   _________________________
  //   A1: 0 1 0 1 0 1 0 1 0 1 0 1 0 1 0 1
  //   _________________________
  //   B2: 0 0 0 0 0 0 0 0 1 1 1 1 1 1 1 1
  //   _________________________
  //   B1: 0 0 0 0 1 1 1 1 0 0 0 0 1 1 1 1
  //   _________________________
  //   _________________________
  //   Q1: 1 1 1 1 0 0 1 1 0 0 0 0 0 0 0 0
  //   _________________________
  //   Q2: 1 1 1 1 0 0 1 1 0 0 0 0 0 0 0 0
  //   Q1 = B2'B1' + A1B2' + A2B1' + A2A1
  //   Q2 = B2'B1' + A2B2'
endmodule

module _3_bit_divider (
  input  a,
  input  b,
  input  c,
  input  d,
  input  e,
  input  f,
  output out_7,
  output out_8,
  output out_9
);

  wire and_1_out, and_2_out, not_1_out, not_2_out, not_3_out, not_4_out, not_5_out;

  not not_1 (not_1_out, f);
  not not_2 (not_2_out, e);
  not not_3 (not_3_out, d);
  and and_1 (and_1_out, not_3_out, not_2_out, not_1_out);
  not not_4 (not_4_out, d);
  not not_5 (not_5_out, e);
  and and_2 (and_2_out, a, not_4_out, not_5_out);
  _2_bit_divider u_2_bit_divider_1 (.A2(b), .A1(c), .B2(e), .B1(f), .Q1(out_7), .Q2(out_8));
  or or_1 (out_9, and_2_out, and_1_out);
endmodule

module _4_bit_divider (
  input  A4,
  input  A3,
  input  A2,
  input  A1,
  input  B4,
  input  B3,
  input  B2,
  input  B1
);

  wire _0000_out, _0001_out, _0010_out, _0011_out, _0100_out, _0101_out, _0110_out, and_1_out, and_2_out,
       and_3_out, and_4_out, and_5_out, and_6_out, and_7_out, and_8_out, and_9_out, and_10_out, and_11_out,
       and_12_out, and_13_out, and_14_out, and_15_out, and_16_out, and_17_out, and_18_out, and_19_out,
       and_20_out, and_21_out, and_22_out, and_23_out, and_24_out, n3_1_q0, n3_1_q1, n3_1_q2, n5_1_q0,
       n5_1_q1, n6_1_q0, n6_1_q1, not_1_out, not_2_out, not_3_out, not_4_out, not_5_out, not_6_out,
       not_7_out, not_8_out, not_9_out, not_10_out, not_11_out, not_12_out, not_13_out, not_14_out,
       not_15_out, not_16_out, not_17_out, not_18_out, not_19_out;

  not not_1 (not_1_out, B1);
  not not_2 (not_2_out, B2);
  not not_3 (not_3_out, B3);
  not not_4 (not_4_out, B4);
  not not_5 (not_5_out, B2);
  not not_6 (not_6_out, B3);
  not not_7 (not_7_out, B4);
  not not_8 (not_8_out, B1);
  not not_9 (not_9_out, B3);
  not not_10 (not_10_out, B4);
  not not_11 (not_11_out, B3);
  not not_12 (not_12_out, B4);
  not not_13 (not_13_out, B1);
  not not_14 (not_14_out, B2);
  not not_15 (not_15_out, B4);
  not not_16 (not_16_out, B2);
  not not_17 (not_17_out, B4);
  not not_18 (not_18_out, B1);
  not not_19 (not_19_out, B4);
  and _0000 (_0000_out, not_1_out, not_2_out, not_3_out, not_4_out);
  and _0001 (_0001_out, B1, not_5_out, not_6_out, not_7_out);
  and _0010 (_0010_out, not_8_out, B2, not_9_out, not_10_out);
  and _0011 (_0011_out, B1, B2, not_11_out, not_12_out);
  and _0100 (_0100_out, not_13_out, not_14_out, B3, not_15_out);
  and _0101 (_0101_out, B1, not_16_out, B3, not_17_out);
  and _0110 (_0110_out, not_18_out, B2, B3, not_19_out);
  and and_1 (and_1_out, _0001_out, A1);
  and and_2 (and_2_out, _0001_out, A2);
  and and_3 (and_3_out, _0001_out, A3);
  and and_4 (and_4_out, _0001_out, A4);
  and and_5 (and_5_out, _0010_out, A2);
  and and_6 (and_6_out, _0010_out, A3);
  and and_7 (and_7_out, _0010_out, A4);
  and and_8 (and_8_out, _0010_out, 1'b0);
  and and_9 (and_9_out, _0011_out, A1);
  and and_10 (and_10_out, _0011_out, A2);
  and and_11 (and_11_out, _0011_out, A3);
  and and_12 (and_12_out, _0011_out, A4);
  and and_13 (and_13_out, _0100_out, A3);
  and and_14 (and_14_out, _0100_out, A4);
  and and_15 (and_15_out, _0100_out, 1'b0);
  and and_16 (and_16_out, _0100_out, 1'b0);
  and and_17 (and_17_out, _0101_out, A1);
  and and_18 (and_18_out, _0101_out, A2);
  and and_19 (and_19_out, _0101_out, A3);
  and and_20 (and_20_out, _0101_out, A4);
  and and_21 (and_21_out, _0110_out, A1);
  and and_22 (and_22_out, _0110_out, A2);
  and and_23 (and_23_out, _0110_out, A3);
  and and_24 (and_24_out, _0110_out, A4);
  _3 u_3_1 (
    .A0(and_9_out), .A1(and_10_out), .A2(and_11_out), .A3(and_12_out), .q0(n3_1_q0), .q1(n3_1_q1),
    .q2(n3_1_q2));  // open: Enable
  _5 u_5_1 (
    .A0(and_17_out), .A1(and_18_out), .A2(and_19_out), .A3(and_20_out), .q0(n5_1_q0), .q1(n5_1_q1));  // open: Enable
  _6 u_6_1 (
    .A0(and_21_out), .A1(and_22_out), .A2(and_23_out), .A3(and_24_out), .q0(n6_1_q0), .q1(n6_1_q1));  // open: Enable
endmodule

module _4_bit_divider_organized (
  input  [3:0] B,
  input  A4,
  input  A3,
  input  A2,
  input  A1
);

  Decoder #(.select(4), .enable("false")) decoder_1 (.sel(B));  // open: out0, out1, out2, out3, out4, out5, out6, out7, out8, out9, out10, out11, out12, out13, out14, out15
endmodule

module _2_and__4_and__8 (
  input  A4,
  input  A3,
  input  A2,
  input  A1,
  input  _2,
  input  _4,
  input  _8,
  output q0,
  output q1,
  output q2
);

  wire and_1_out, and_2_out, and_3_out, and_4_out, and_5_out;

  and and_1 (and_1_out, A2, _2);
  and and_2 (and_2_out, A3, _4);
  and and_3 (and_3_out, A4, _8);
  and and_4 (and_4_out, A3, _2);
  and and_5 (and_5_out, A4, _4);
  and and_6 (q2, A4, _2);
  or or_1 (q0, and_1_out, and_2_out, and_3_out);
  or or_2 (q1, and_4_out, and_5_out);
endmodule

module _3 (
  input  Enable,
  input  A0,
  input  A1,
  input  A2,
  input  A3,
  output q0,
  output q1,
  output q2
);

  wire and_1_out, and_2_out, and_3_out, and_4_out, and_5_out, and_6_out, and_7_out, and_8_out, not_1_out,
       not_2_out, not_3_out, not_4_out, not_5_out, not_6_out, not_7_out, or_1_out, or_2_out;

  not not_1 (not_1_out, A2);
  not not_2 (not_2_out, A1);
  not not_3 (not_3_out, A3);
  not not_4 (not_4_out, A1);
  not not_5 (not_5_out, A2);
  not not_6 (not_6_out, A3);
  not not_7 (not_7_out, A2);
  and and_1 (and_1_out, not_1_out, A1, A0);
  and and_2 (and_2_out, not_2_out, A2, not_3_out);
  and and_3 (and_3_out, A3, not_4_out, A0);
  and and_4 (and_4_out, A3, not_5_out, A1);
  and and_5 (and_5_out, A0, A1, A3);
  and and_6 (and_6_out, not_6_out, A2, A1);
  and and_7 (and_7_out, A3, not_7_out);
  or or_1 (or_1_out, and_1_out, and_2_out, and_3_out, and_4_out, and_5_out);
  or or_2 (or_2_out, and_6_out, and_7_out);
  and and_8 (and_8_out, A2, A3);
  and and_9 (q0, Enable, or_1_out);
  and and_10 (q1, Enable, or_2_out);
  and and_11 (q2, Enable, and_8_out);

  // Notes on the sheet:
  //   A0A1A2A3
endmodule

module _5 (
  input  Enable,
  input  A0,
  input  A1,
  input  A2,
  input  A3,
  output q0,
  output q1
);

  wire and_1_out, and_2_out, and_3_out, and_4_out, and_5_out, and_6_out, not_1_out, not_2_out, not_3_out,
       not_4_out, or_1_out, or_2_out;

  not not_1 (not_1_out, A3);
  not not_2 (not_2_out, A3);
  not not_3 (not_3_out, A1);
  not not_4 (not_4_out, A2);
  and and_1 (and_1_out, not_1_out, A2, A0);
  and and_2 (and_2_out, not_2_out, A2, A1);
  and and_3 (and_3_out, A3, not_3_out, not_4_out);
  and and_4 (and_4_out, A2, A1, A0);
  and and_5 (and_5_out, A3, A1);
  and and_6 (and_6_out, A3, A2);
  or or_1 (or_1_out, and_1_out, and_2_out, and_3_out, and_4_out);
  or or_2 (or_2_out, and_5_out, and_6_out);
  and and_7 (q0, Enable, or_1_out);
  and and_8 (q1, Enable, or_2_out);
endmodule

module _6 (
  input  Enable,
  input  A0,
  input  A1,
  input  A2,
  input  A3,
  output q0,
  output q1
);

  wire and_1_out, and_2_out, and_3_out, not_1_out, not_2_out, or_1_out;

  not not_1 (not_1_out, A3);
  and and_1 (and_1_out, not_1_out, A2, A1);
  and and_2 (and_2_out, A3, not_2_out);
  not not_2 (not_2_out, A2);
  and and_3 (and_3_out, A2, A3);
  or or_1 (or_1_out, and_1_out, and_2_out);
  and and_4 (q0, Enable, or_1_out);
  and and_5 (q1, Enable, and_3_out);
endmodule
